// Logisim project Assignment8.circ as structural Verilog: 4 circuits, main circuit Circuit 1
module Circuit_1 (
  input  A,
  input  B,
  input  C,
  output X
);

  wire and_1_out, nor_1_out;

  nor nor_1 (nor_1_out, A, B);
  and and_1 (and_1_out, A, C, C);
  ExactlyOne xor_1 (.out(X), .in0(nor_1_out), .in1(nor_1_out), .in3(and_1_out));
endmodule

module Circuit_2 (
  input  A,
  input  B,
  input  C,
  input  D,
  output Y
);

  wire and_1_out, nand_1_out, or_1_out;

  or or_1 (or_1_out, A, B, B);
  nand nand_1 (nand_1_out, C, D);
  and and_1 (and_1_out, or_1_out, or_1_out, nand_1_out, nand_1_out);
  not nor_1 (Y, and_1_out);  // NOR_Gate
endmodule

module Circuit_3 (
  input  A,
  input  B,
  input  C,
  input  D,
  input  E,
  output Z
);

  wire and_1_out, nor_1_out, or_1_out, xor_1_out;

  and and_1 (and_1_out, A, B, B);
  xor xor_1 (xor_1_out, C, D);
  nor nor_1 (nor_1_out, and_1_out, and_1_out, xor_1_out);
  or or_1 (or_1_out, D, E);
  and and_2 (Z, nor_1_out, or_1_out, or_1_out);
endmodule

module Circuit_4 (
  input  C,
  input  D,
  input  E,
  output w
);

  wire and_1_out, and_2_out, and_3_out;

  and and_1 (and_1_out, D, E);
  and and_2 (and_2_out, C, E);
  and and_3 (and_3_out, C, D);
  or or_1 (w, and_1_out, and_2_out, and_3_out);
endmodule
